// Logisim project ALU.circ as structural Verilog: 10 circuits, main circuit ALU
module ALU (
  input  [15:0] A,
  input  [15:0] B,
  input  [2:0] S,
  output [15:0] out_4,
  output Overflow,
  output div_0,
  output Underflow
);

  wire div_1_div_0, mult_1_overflow, mult_1_underflow, sub_1_overflow, sub_1_underflow, sum_1_overflow,
       sum_1_underflow;
  wire [15:0] div_1_quociente, div_1_resto, mult_1_resultado, sub_1_resultado, sum_1_resultado;

  Pull_Resistor pull_resistor_1 (.node(div_0));
  Multiplexer #(.select(3), .enable("false")) multiplexer_1 (
    .in0(1'b0), .in1(1'b0), .in2(1'b0), .in3(div_1_div_0), .in4(div_1_div_0), .in5(1'b0), .in6(1'b0),
    .in7(1'b0), .out(div_0), .sel(S));
  Sum sum_1 (.A(A), .B(B), .Resultado(sum_1_resultado), .Underflow(sum_1_underflow), .Overflow(sum_1_overflow));
  Sub sub_1 (
    .Minuendo(A), .Subtraendo(B), .Resultado(sub_1_resultado), .Overflow(sub_1_overflow),
    .Underflow(sub_1_underflow));
  Mult mult_1 (.X(A), .Y(B), .Resultado(mult_1_resultado), .Overflow(mult_1_overflow), .Underflow(mult_1_underflow));
  Div div_1 (.Dividendo(A), .Divisor(B), .Quociente(div_1_quociente), .Resto(div_1_resto), .div_0(div_1_div_0));
  Multiplexer #(.select(3), .enable("false")) multiplexer_2 (
    .in0(sum_1_underflow), .in1(sub_1_underflow), .in2(mult_1_underflow), .in3(1'b0), .in4(1'b0),
    .out(Underflow), .sel(S));  // open: in5, in6, in7
  Multiplexer #(.select(3), .width(16), .enable("false")) multiplexer_3 (
    .in0(sum_1_resultado), .in1(sub_1_resultado), .in2(mult_1_resultado), .in3(div_1_quociente),
    .in4(div_1_resto), .out(out_4), .sel(S));  // open: in5, in6, in7
  Pull_Resistor pull_resistor_2 (.node(Overflow));
  Multiplexer #(.select(3), .enable("false")) multiplexer_4 (
    .in0(sum_1_overflow), .in1(sub_1_overflow), .in2(mult_1_overflow), .in3(1'b0), .in4(1'b0),
    .out(Overflow), .sel(S));  // open: in5, in6, in7
  Pull_Resistor pull_resistor_3 (.node(Underflow));
endmodule

module Sum (
  input  [15:0] A,
  input  [15:0] B,
  output [15:0] Resultado,
  output Overflow,
  output Underflow
);

  wire lastbit_1_out, lastbit_2_out, lastbit_3_out;

  LastBit lastbit_1 (.in_1(B), .Out(lastbit_1_out));
  LastBit lastbit_2 (.in_1(A), .Out(lastbit_2_out));
  Adder #(.width(16)) adder_1 (.a(A), .b(B), .out(Resultado));  // open: cin, cout
  LastBit lastbit_3 (.in_1(Resultado), .Out(lastbit_3_out));
  and and_1 (Overflow, lastbit_3_out, ~lastbit_2_out, ~lastbit_1_out);  // AND_Gate
  and and_2 (Underflow, ~lastbit_3_out, lastbit_2_out, lastbit_1_out);  // AND_Gate
endmodule

module Full_Adder (
  input  cin,
  input  A,
  input  B,
  output r,
  output cout
);

  wire and_1_out, and_2_out, xor_1_out;

  and and_1 (and_1_out, A, B);
  xor xor_1 (xor_1_out, A, B);
  or or_1 (cout, and_1_out, and_2_out);
  and and_2 (and_2_out, cin, xor_1_out);
  xor xor_2 (r, cin, xor_1_out);
endmodule

module Half_Adder (
  input  A,
  input  B,
  output Resultado,
  output Carry
);

  xor xor_1 (Resultado, A, B);
  and and_1 (Carry, A, B);
endmodule

module Comp2 (
  input  [15:0] Entrada,
  output [15:0] Resultado
);

  wire [15:0] not_1_out;

  assign not_1_out = ~Entrada;  // NOT_Gate not_1, 16 bits wide
  Sum sum_1 (.A(16'h1), .B(not_1_out), .Resultado(Resultado));  // open: Underflow, Overflow
endmodule

module Sub (
  input  [15:0] Minuendo,
  input  [15:0] Subtraendo,
  output [15:0] Resultado,
  output Overflow,
  output Underflow
);

  wire [15:0] comp2_1_resultado;

  Comp2 comp2_1 (.Entrada(Subtraendo), .Resultado(comp2_1_resultado));
  Sum sum_1 (.A(Minuendo), .B(comp2_1_resultado), .Resultado(Resultado), .Underflow(Underflow), .Overflow(Overflow));
endmodule

module Mult (
  input  [15:0] X,
  input  [15:0] Y,
  output [15:0] Resultado,
  output Overflow,
  output Underflow
);

  wire or_1_out, xor_1_out;
  wire [15:0] multiplier_1_cout;

  Multiplier #(.width(16)) multiplier_1 (.a(X), .b(Y), .out(Resultado), .cout(multiplier_1_cout));  // open: cin
  or or_1 (or_1_out, multiplier_1_cout[0], multiplier_1_cout[1], multiplier_1_cout[2], multiplier_1_cout[3], multiplier_1_cout[4], multiplier_1_cout[5], multiplier_1_cout[6], multiplier_1_cout[7], multiplier_1_cout[8], multiplier_1_cout[9], multiplier_1_cout[10], multiplier_1_cout[11], multiplier_1_cout[12], multiplier_1_cout[13], multiplier_1_cout[14], multiplier_1_cout[15]);
  xor xor_1 (xor_1_out, X[15], Y[15]);
  and and_1 (Underflow, or_1_out, xor_1_out);
  and and_2 (Overflow, or_1_out, ~Underflow);  // AND_Gate
endmodule

module DivModule (
  input  Y,
  input  X,
  input  Li,
  input  OS,
  output L0,
  output D
);

  wire and_1_out, and_2_out, and_3_out, and_4_out, not_1_out, not_2_out, xnor_1_out, xor_1_out;

  or or_1 (L0, and_1_out, and_2_out);
  ExactlyOne xor_1 (.out(xor_1_out), .in0(Y), .in1(X), .in2(Li));
  not not_1 (not_1_out, OS);
  and and_1 (and_1_out, Y, not_2_out);
  and and_2 (and_2_out, xnor_1_out, Li);
  and and_3 (and_3_out, xor_1_out, not_1_out);
  or or_2 (D, and_3_out, and_4_out);
  not not_2 (not_2_out, X);
  xnor xnor_1 (xnor_1_out, Y, X);
  and and_4 (and_4_out, X, OS);
endmodule

module Div (
  input  [15:0] Dividendo,
  input  [15:0] Divisor,
  output [15:0] Quociente,
  output [15:0] Resto,
  output div_0
);

  nor nor_1 (div_0, Divisor[0], Divisor[1], Divisor[2], Divisor[3], Divisor[4], Divisor[5], Divisor[6], Divisor[7], Divisor[8], Divisor[9], Divisor[10], Divisor[11], Divisor[12], Divisor[13], Divisor[14], Divisor[15]);
  Divider #(.width(16)) divider_1 (.a(Dividendo), .b(Divisor), .out(Quociente), .rem(Resto));  // open: upper
endmodule

module LastBit (
  input  [15:0] in_1,
  output Out
);


  assign Out = in_1[15];
endmodule
