// Logisim project EP3.circ as structural Verilog: 4 circuits, main circuit main
module PC (
  input  [7:0] Input_Address,
  input  Set,
  input  Reset,
  input  Counter_UP,
  output [7:0] Output_Address
);

  wire and_1_out, and_2_out, and_3_out, and_4_out, and_5_out, and_6_out, and_7_out, and_8_out, and_9_out,
       and_10_out, and_11_out, and_12_out, and_13_out, and_14_out, and_15_out, and_16_out, j_k_ff_1_qn,
       j_k_ff_2_qn, j_k_ff_3_qn, j_k_ff_4_qn, j_k_ff_5_qn, j_k_ff_6_qn, j_k_ff_7_qn, or_1_out, or_2_out,
       or_3_out, or_4_out, or_5_out, or_6_out, or_7_out, or_8_out;

  and and_1 (and_1_out, Set, Input_Address[0]);
  J_K_Flip_Flop j_k_ff_1 (
    .J(1'b1), .clk(Counter_UP), .K(1'b1), .Q(Output_Address[0]), .Qn(j_k_ff_1_qn), .preset(and_1_out),
    .en(1'b1), .reset(or_2_out));
  and and_2 (and_2_out, Set, Input_Address[1]);
  and and_3 (and_3_out, Set, ~Input_Address[0]);  // AND_Gate
  or or_1 (or_1_out, Reset, and_5_out);
  or or_2 (or_2_out, Reset, and_3_out);
  J_K_Flip_Flop j_k_ff_2 (
    .J(1'b1), .clk(j_k_ff_1_qn), .K(1'b1), .Q(Output_Address[1]), .Qn(j_k_ff_2_qn), .preset(and_2_out),
    .en(1'b1), .reset(or_1_out));
  and and_4 (and_4_out, Set, Input_Address[2]);
  and and_5 (and_5_out, Set, ~Input_Address[1]);  // AND_Gate
  and and_6 (and_6_out, Set, ~Input_Address[2]);  // AND_Gate
  or or_3 (or_3_out, Reset, and_6_out);
  and and_7 (and_7_out, Set, ~Input_Address[3]);  // AND_Gate
  and and_8 (and_8_out, Set, Input_Address[3]);
  or or_4 (or_4_out, Reset, and_7_out);
  J_K_Flip_Flop j_k_ff_3 (
    .J(1'b1), .clk(j_k_ff_2_qn), .K(1'b1), .Q(Output_Address[2]), .Qn(j_k_ff_3_qn), .preset(and_4_out),
    .en(1'b1), .reset(or_3_out));
  and and_9 (and_9_out, Set, Input_Address[4]);
  and and_10 (and_10_out, Set, ~Input_Address[4]);  // AND_Gate
  or or_5 (or_5_out, Reset, and_10_out);
  J_K_Flip_Flop j_k_ff_4 (
    .J(1'b1), .clk(j_k_ff_3_qn), .K(1'b1), .Q(Output_Address[3]), .Qn(j_k_ff_4_qn), .preset(and_8_out),
    .en(1'b1), .reset(or_4_out));
  and and_11 (and_11_out, Set, Input_Address[5]);
  and and_12 (and_12_out, Set, ~Input_Address[5]);  // AND_Gate
  or or_6 (or_6_out, Reset, and_12_out);
  J_K_Flip_Flop j_k_ff_5 (
    .J(1'b1), .clk(j_k_ff_4_qn), .K(1'b1), .Q(Output_Address[4]), .Qn(j_k_ff_5_qn), .preset(and_9_out),
    .en(1'b1), .reset(or_5_out));
  and and_13 (and_13_out, Set, Input_Address[7]);
  and and_14 (and_14_out, Set, Input_Address[6]);
  and and_15 (and_15_out, Set, ~Input_Address[6]);  // AND_Gate
  or or_7 (or_7_out, Reset, and_15_out);
  J_K_Flip_Flop j_k_ff_6 (
    .J(1'b1), .clk(j_k_ff_5_qn), .K(1'b1), .Q(Output_Address[5]), .Qn(j_k_ff_6_qn), .preset(and_11_out),
    .en(1'b1), .reset(or_6_out));
  and and_16 (and_16_out, Set, ~Input_Address[7]);  // AND_Gate
  or or_8 (or_8_out, Reset, and_16_out);
  J_K_Flip_Flop j_k_ff_7 (
    .J(1'b1), .clk(j_k_ff_6_qn), .K(1'b1), .Q(Output_Address[6]), .Qn(j_k_ff_7_qn), .preset(and_14_out),
    .en(1'b1), .reset(or_7_out));
  J_K_Flip_Flop j_k_ff_8 (
    .J(1'b1), .clk(j_k_ff_7_qn), .K(1'b1), .Q(Output_Address[7]), .preset(and_13_out), .en(1'b1),
    .reset(or_8_out));  // open: Qn
endmodule

module CTRL (
  input  Entradas,
  input  in_2,
  input  in_3,
  input  [7:0] in_4,
  input  [15:0] IR_OUT,
  input  [15:0] ACC_OUT,
  output RAM_CLOCK,
  output CU,
  output RAM_LD,
  output IR_EN,
  output PRN_EN,
  output ACC_EN,
  output OP,
  output PC_SET,
  output [2:0] S,
  output [7:0] PC_IN,
  output [7:0] RAM_ADDRESS,
  output READING,
  output [15:0] OUT
);

  wire ADD, and_7_out, cmp_3_out_4, cmp_4_out_4, cmp_5_out_4, cmp_6_out_4, cmp_7_out_4, cmp_8_out_4,
       comparator_1_gt, comparator_2_eq, comparator_3_gt, comparator_4_eq, comparator_5_lt, comparator_6_lt,
       DIV, ENABLE, JDZ, JEQ, JGE, JGT, JLE, JLT, JMP, LDA, MUL, NOP, not_1_out, not_2_out, not_3_out,
       not_4_out, or_2_out, or_3_out, REM, STA, STOP, SUB;
  wire [1:0] counter_1_q;

  CMP cmp_1 (.in_1(IR_OUT[7:0]), .in_2(8'hb), .out_4(LDA), .Enable(ENABLE));
  CMP cmp_2 (.in_1(IR_OUT[7:0]), .in_2(8'h32), .out_4(NOP), .Enable(ENABLE));
  CMP cmp_3 (.in_1(IR_OUT[7:0]), .in_2(8'h34), .out_4(cmp_3_out_4), .Enable(ENABLE));
  CMP cmp_4 (.in_1(IR_OUT[7:0]), .in_2(8'h35), .out_4(cmp_4_out_4), .Enable(ENABLE));
  CMP cmp_5 (.in_1(IR_OUT[7:0]), .in_2(8'h36), .out_4(cmp_5_out_4), .Enable(ENABLE));
  CMP cmp_6 (.in_1(IR_OUT[7:0]), .in_2(8'h37), .out_4(cmp_6_out_4), .Enable(ENABLE));
  CMP cmp_7 (.in_1(IR_OUT[7:0]), .in_2(8'h38), .out_4(cmp_7_out_4), .Enable(ENABLE));
  CMP cmp_8 (.in_1(IR_OUT[7:0]), .in_2(8'h39), .out_4(cmp_8_out_4), .Enable(ENABLE));
  CMP cmp_9 (.in_1(IR_OUT[7:0]), .in_2(8'h33), .out_4(JMP), .Enable(ENABLE));
  Comparator #(.width(16)) comparator_1 (.a(ACC_OUT), .b({16{1'b0}}), .gt(comparator_1_gt));  // open: eq, lt
  Comparator #(.width(16)) comparator_2 (.a(ACC_OUT), .b({16{1'b0}}), .eq(comparator_2_eq));  // open: gt, lt
  Comparator #(.width(16)) comparator_3 (.a(ACC_OUT), .b({16{1'b0}}), .gt(comparator_3_gt));  // open: eq, lt
  Comparator #(.width(16)) comparator_4 (.a(ACC_OUT), .b({16{1'b0}}), .eq(comparator_4_eq));  // open: gt, lt
  Comparator #(.width(16)) comparator_5 (.a(ACC_OUT), .b({16{1'b0}}), .lt(comparator_5_lt));  // open: gt, eq
  Comparator #(.width(16)) comparator_6 (.a(ACC_OUT), .b({16{1'b0}}), .lt(comparator_6_lt));  // open: gt, eq
  CMP cmp_10 (.in_1(IR_OUT[7:0]), .in_2(8'hc), .out_4(STA), .Enable(ENABLE));
  CMP cmp_11 (.in_1(IR_OUT[7:0]), .in_2(8'h46), .out_4(STOP), .Enable(ENABLE));
  and and_1 (JLE, cmp_3_out_4, ~comparator_1_gt);  // AND_Gate
  and and_2 (JDZ, cmp_4_out_4, ~comparator_2_eq);  // AND_Gate
  and and_3 (JGT, cmp_5_out_4, comparator_3_gt);
  and and_4 (JEQ, cmp_6_out_4, comparator_4_eq);
  and and_5 (JLT, cmp_7_out_4, comparator_5_lt);
  and and_6 (JGE, cmp_8_out_4, ~comparator_6_lt);  // AND_Gate
  CMP cmp_12 (.in_1(IR_OUT[7:0]), .in_2(8'h1f), .out_4(READING), .Enable(ENABLE));
  CMP cmp_13 (.in_1(IR_OUT[7:0]), .in_2(8'h29), .out_4(PRN_EN), .Enable(ENABLE));
  or or_1 (ACC_EN, LDA, OP);
  CMP cmp_14 (.in_1(IR_OUT[7:0]), .in_2(8'h15), .out_4(ADD), .Enable(ENABLE));
  CMP cmp_15 (.in_1(IR_OUT[7:0]), .in_2(8'h16), .out_4(SUB), .Enable(ENABLE));
  CMP cmp_16 (.in_1(IR_OUT[7:0]), .in_2(8'h17), .out_4(MUL), .Enable(ENABLE));
  CMP cmp_17 (.in_1(IR_OUT[7:0]), .in_2(8'h18), .out_4(DIV), .Enable(ENABLE));
  CMP cmp_18 (.in_1(IR_OUT[7:0]), .in_2(8'h19), .out_4(REM), .Enable(ENABLE));
  Transistor #(.\type ("n"), .width(3)) transistor_1 (.in(3'b000), .out(S), .gate(ADD));
  Transistor #(.\type ("n"), .width(3)) transistor_2 (.in(3'b001), .out(S), .gate(SUB));
  Transistor #(.\type ("n"), .width(3)) transistor_3 (.in(3'b010), .out(S), .gate(MUL));
  Transistor #(.\type ("n"), .width(3)) transistor_4 (.in(3'b011), .out(S), .gate(DIV));
  Transistor #(.\type ("n"), .width(3)) transistor_5 (.in(3'b100), .out(S), .gate(REM));
  nor nor_1 (RAM_LD, STA, READING);
  or or_2 (or_2_out, LDA, STA, PRN_EN, READING, OP);
  Transistor #(.width(8)) transistor_6 (.in(in_4), .out(RAM_ADDRESS), .gate(or_2_out));
  or or_3 (or_3_out, READING, STA);
  not not_1 (not_1_out, Entradas);
  not not_2 (not_2_out, not_3_out);
  not not_3 (not_3_out, not_1_out);
  and and_7 (and_7_out, ~in_3, ~STOP, ~Entradas);  // AND_Gate
  or or_4 (PC_SET, JMP, JLE, JDZ, JGT, JEQ, JLT, JGE);
  or or_5 (OP, ADD, SUB, MUL, DIV, REM);
  Transistor #(.\type ("n"), .width(8)) transistor_7 (.in(IR_OUT[15:8]), .out(RAM_ADDRESS), .gate(or_2_out));
  Transistor #(.gate("br")) transistor_8 (.in(Entradas), .out(RAM_CLOCK), .gate(or_3_out));
  Transistor #(.\type ("n")) transistor_9 (.in(not_4_out), .out(RAM_CLOCK), .gate(or_3_out));
  not not_4 (not_4_out, not_2_out);
  Demultiplexer #(.select(2), .enable("false")) demultiplexer_1 (
    .out0(IR_EN), .out1(CU), .out2(ENABLE), .in(1'b1), .sel(counter_1_q));  // open: out3
  Counter #(.width(2), .max('h2)) counter_1 (
    .Q(counter_1_q), .clk(and_7_out), .clr(in_2));  // open: load, D, count, carry

  assign PC_IN = IR_OUT[15:8];

  // Other names for the same wires on the sheet: CLOCK = Entradas; ERROR = in_3; INN = READING;
  //   COD[7:0] = IR_OUT[7:0]; IR_ADDR[7:0] = IR_OUT[15:8]; JUMP = PC_SET; MATH = OP; OUTPUT[15:0] = OUT;
  //   PC_OUT[7:0] = in_4; PRN = PRN_EN; RESET = in_2

  // Notes on the sheet:
  //   LDA - 11
  //   NOP - 50
  //   Jumps
  //   JMP - 51
  //   JLE - 52
  //   JDZ - 53
  //   JGT - 54
  //   JEQ - 55
  //   JLT - 56
  //   JGE - 57
  //   Instruções
  //   STA - 12
  //   STP - 70
  //   INN - 31
  //   PRN - 41
  //   Aritimética
  //   ADD - 21
  //   SUB - 22
  //   MUL - 23
  //   DIV - 24
  //   REM - 25
  //   Saídas
  //   JMP - PC_SET
  //   É operação
  //   Selecionar acesso à RAM
  //   RAM Clock
  //   Ciclo de Instrução
endmodule

module CMP (
  input  [7:0] in_1,
  input  [7:0] in_2,
  input  Enable,
  output out_4
);

  wire and_1_out;
  wire [7:0] xnor_1_out;

  assign xnor_1_out = ~(in_1 ^ in_2);  // XNOR_Gate xnor_1, 8 bits wide
  and and_1 (and_1_out, xnor_1_out[0], xnor_1_out[1], xnor_1_out[2], xnor_1_out[3], xnor_1_out[4], xnor_1_out[5], xnor_1_out[6], xnor_1_out[7]);
  and and_2 (out_4, and_1_out, Enable);
endmodule

module main (
  input  [15:0] in_1
);

  wire ACC_EN, alu_1_div_0, alu_1_overflow, alu_1_underflow, CLOCK, CU, ERROR, IR_EN, OP, PC_SET, PRN_EN,
       RAM_CLOCK, RAM_LOAD, READING, RESET;
  wire [2:0] S;
  wire [7:0] PC_IN, PC_OUT, RAM_ADDR;
  wire [15:0] ACC_OUT, ALU_OUT, IR_OUT, OUT, Output_q, RAM_OUT, transistor_1_out, transistor_3_out,
       transistor_4_out, transistor_7_out;

  Button button_1 (.out(RESET));
  Clock clock_1 (.out(CLOCK));
  Register #(.width(16)) Output (.D(RAM_OUT), .en(PRN_EN), .Q(Output_q), .clk(CLOCK), .clr(RESET));
  Hex_Digit_Display hex_digit_display_1 (.value(Output_q[11:8]));  // open: dp
  Hex_Digit_Display hex_digit_display_2 (.value(Output_q[15:12]));  // open: dp
  CTRL ctrl_1 (
    .IR_OUT(IR_OUT), .RAM_LD(RAM_LOAD), .IR_EN(IR_EN), .CU(CU), .RAM_CLOCK(RAM_CLOCK), .Entradas(CLOCK),
    .in_2(RESET), .PC_IN(PC_IN), .PC_SET(PC_SET), .RAM_ADDRESS(RAM_ADDR), .in_4(PC_OUT), .ACC_EN(ACC_EN),
    .ACC_OUT(ACC_OUT), .S(S), .OP(OP), .OUT(OUT), .PRN_EN(PRN_EN), .READING(READING), .in_3(ERROR));
  Hex_Digit_Display hex_digit_display_3 (.value(Output_q[3:0]));  // open: dp
  Hex_Digit_Display hex_digit_display_4 (.value(Output_q[7:4]));  // open: dp
  Hex_Digit_Display hex_digit_display_5 (.value(in_1[15:12]));  // open: dp
  Hex_Digit_Display hex_digit_display_6 (.value(in_1[11:8]));  // open: dp
  Hex_Digit_Display hex_digit_display_7 (.value(in_1[7:4]));  // open: dp
  Hex_Digit_Display hex_digit_display_8 (.value(in_1[3:0]));  // open: dp
  Transistor #(.width(16)) transistor_1 (.in(RAM_OUT), .out(transistor_1_out), .gate(OP));
  Transistor #(.\type ("n"), .width(16)) transistor_2 (.in(ALU_OUT), .out(transistor_1_out), .gate(OP));
  Register #(.width(16)) ACC (.D(transistor_1_out), .en(ACC_EN), .Q(ACC_OUT), .clk(CLOCK), .clr(RESET));
  Transistor #(.width(16)) transistor_3 (.in(transistor_4_out), .out(transistor_3_out), .gate(RAM_LOAD));
  Transistor #(.gate("br"), .width(16)) transistor_4 (.in(ACC_OUT), .out(transistor_4_out), .gate(READING));
  RAM #(.dataWidth(16)) ram_1 (
    .addr(RAM_ADDR), .data(transistor_3_out), .sel(1'b1), .clk(RAM_CLOCK), .ld(RAM_LOAD));  // open: clr
  Transistor #(.\type ("n"), .width(16)) transistor_5 (.in(in_1), .out(transistor_4_out), .gate(READING));
  Transistor #(.\type ("n"), .gate("br"), .width(16)) transistor_6 (
    .in(transistor_3_out), .out(RAM_OUT), .gate(RAM_LOAD));
  Register #(.width(16)) IR (.D(RAM_OUT), .en(IR_EN), .Q(IR_OUT), .clk(CLOCK), .clr(RESET));
  Transistor #(.\type ("n"), .width(16)) transistor_7 (.in(ACC_OUT), .out(transistor_7_out), .gate(RAM_LOAD));
  PC pc_1 (.Set(PC_SET), .Reset(RESET), .Counter_UP(CU), .Input_Address(PC_IN), .Output_Address(PC_OUT));
  ALU alu_1 (
    .Overflow(alu_1_overflow), .A(transistor_7_out), .B(RAM_OUT), .S(S), .out_4(ALU_OUT),
    .div_0(alu_1_div_0), .Underflow(alu_1_underflow));
  or or_1 (ERROR, alu_1_overflow, alu_1_underflow, alu_1_div_0);

  // Other names for the same wires on the sheet: INPUT[15:0] = in_1

  // Notes on the sheet:
  //   Início
  //   RAM
endmodule
